# Fritzing sketch xiao-breadboard (saved by Fritzing 1.0.8)
breadboards: 1

parts:
  XIAO_ESP32S3 = XIAO ESP32S3 [package="DIP (Dual Inline) [THT]"]
  R1_1k_base = resistor [resistance=1000 package=THT]
  Q1_2N3904_E_B_C = TRANSISTOR_NPN [package=to-92]
  R2_1k_bench_LED = resistor [resistance=1000 package=THT]
  LED1_steady_bench_load = Red LED - 5mm [package="5 mm [THT]"]
  R3_100k_pulldown = resistor [resistance=100000 package=THT]
  R4_1k_hold_LED = resistor [resistance=1000 package=THT]
  LED2_blinking_hold_indicator = Red LED - 5mm [package="5 mm [THT]"]

nets:
  N1: XIAO_ESP32S3.D0, R4_1k_hold_LED.Pin_1
  N2: XIAO_ESP32S3.D10, R1_1k_base.Pin_0
  N3: XIAO_ESP32S3.3V3, R2_1k_bench_LED.Pin_1
  N4: XIAO_ESP32S3.GND, Q1_2N3904_E_B_C.E, R3_100k_pulldown.Pin_1, LED2_blinking_hold_indicator.cathode
  N5: R1_1k_base.Pin_1, Q1_2N3904_E_B_C.B, R3_100k_pulldown.Pin_0
  N6: Q1_2N3904_E_B_C.C, LED1_steady_bench_load.cathode
  N7: R2_1k_bench_LED.Pin_0, LED1_steady_bench_load.anode
  N8: R4_1k_hold_LED.Pin_0, LED2_blinking_hold_indicator.anode

custom parts:
  XIAO ESP32S3: Seeed Studio XIAO ESP32S3 leverages 240MHz Xtensa 32-bit LX7 dual-core processor, supporting both WiFi and BLE 5.0 wireless connectivities, a 2.4GHz Rod antenna, allows for deep sleep mode with power consumption as low as 14μA while supporting lithium battery charging management. Ideal for the Internet of Things, Smart Homes, Wireless wearable devices, Robotics, etc.
  1000 ohm resistor: A generic resistor (0.25W)
  TRANSISTOR_NPN: Generic NPN BJT. MMBT2222 is the common NPN we use. Double check against datasheet- not all devices are the same!
  1000 ohm resistor: A generic resistor (0.25W)
  Red LED - 5mm: A generic red LED (~1.8V)
  100000 ohm resistor: A generic resistor (0.25W)
  1000 ohm resistor: A generic resistor (0.25W)
  Red LED - 5mm: A generic red LED (~1.8V)
